# Fritzing sketch photon2-wire-diagram (saved by Fritzing 0.9.2b)
breadboards: 1

parts:
  Part1 = Photon
  DS1 = DS18B20 1-Wire Temperature Sensor [part_number=DS18B20]
  R1 = Resistor [tolerance=±5% resistance=1k package="0805 [SMD]"]
  J1 = Piezo Speaker
  LED1 = smd LED [color="Red (633nm)" package="0805 [SMD]"]
  LED2 = smd LED [color="Green (555nm)" package="0805 [SMD]"]
  PIR1 = PIR sensor
  R2 = Resistor [tolerance=±5% resistance=1k package="0805 [SMD]"]
  OLED1 = 128x64 Monochrom OLED Display with SPI Control

nets:
  N1: Part1.A0, PIR1.SIG
  N2: Part1.A3, OLED1.Clock
  N3: Part1.A5, OLED1.Data
  GND: Part1.GND, J1.pin1, PIR1.GND, R2.Pin_0, OLED1.GND
  VIN: Part1.VIN, PIR1.VDD, OLED1.Vin
  N4: Part1.D0, R1.Pin_0
  N5: Part1.D1, LED1.anode
  N6: Part1.D2, LED2.anode
  N7: Part1.D3, OLED1.SA0/DC
  N8: Part1.D4, OLED1.CS
  N9: Part1.D5, OLED1.Reset
  3V3: Part1.3V3, DS1.VDD
  N10: DS1.GND, J1.pin2
  N11: DS1.DQ, R1.Pin_1
  N12: LED1.cathode, LED2.cathode, R2.Pin_1

notes:
  OLED Mapping:
  GND -> GND
  VCC -> VIN
  D0 -> A3
  D1 - A5
  RST -> D5
  DC -> D3
  CS -> D4
